// Logisim project Avaliação-Arquitetura.circ as structural Verilog: 1 circuit, main circuit main
module main (
  input  A,
  input  B,
  input  C,
  input  D,
  input  C1,
  input  C2,
  input  in_7,
  input  in_8,
  input  in_9,
  input  in_10,
  input  in_11,
  input  in_12,
  input  in_13,
  input  in_14,
  input  in_15,
  input  in_16,
  output out_17,
  output out_18,
  output out_19,
  output out_20,
  output out_21,
  output out_22
);

  wire and_1_out, and_2_out, and_3_out, and_4_out, and_5_out, and_6_out, and_7_out, and_8_out, and_9_out,
       and_10_out, and_11_out, and_12_out, not_1_out, not_2_out, not_3_out, not_4_out, or_1_out, or_2_out,
       or_4_out, or_5_out, or_6_out, or_7_out, or_8_out, xor_1_out, xor_2_out, xor_4_out, xor_5_out,
       xor_7_out, xor_8_out, xor_10_out, xor_11_out;

  and and_1 (and_1_out, in_15, in_7);
  xor xor_1 (xor_1_out, in_8, in_16);
  or or_1 (or_1_out, in_15, in_7);
  xor xor_2 (xor_2_out, in_8, in_7);
  and and_2 (and_2_out, xor_1_out, or_1_out);
  not not_1 (not_1_out, C1);
  not not_2 (not_2_out, C2);
  not not_3 (not_3_out, C1);
  not not_4 (not_4_out, C2);
  xor xor_3 (out_18, xor_2_out, in_15);
  or or_2 (or_2_out, and_1_out, and_2_out);
  and and_3 (and_3_out, A, not_1_out, not_2_out);
  and and_4 (and_4_out, B, not_3_out, C2);
  and and_5 (and_5_out, C, C1, not_4_out);
  and and_6 (and_6_out, D, C1, C2);
  or or_3 (out_17, and_3_out, and_4_out, and_5_out, and_6_out);
  xor xor_4 (xor_4_out, in_10, in_9);
  and and_7 (and_7_out, or_2_out, in_9);
  xor xor_5 (xor_5_out, in_10, in_16);
  or or_4 (or_4_out, or_2_out, in_9);
  xor xor_6 (out_19, xor_4_out, or_2_out);
  and and_8 (and_8_out, xor_5_out, or_4_out);
  or or_5 (or_5_out, and_7_out, and_8_out);
  xor xor_7 (xor_7_out, in_12, in_11);
  and and_9 (and_9_out, or_5_out, in_11);
  xor xor_8 (xor_8_out, in_12, in_16);
  or or_6 (or_6_out, or_5_out, in_11);
  xor xor_9 (out_20, xor_7_out, or_5_out);
  and and_10 (and_10_out, xor_8_out, or_6_out);
  or or_7 (or_7_out, and_9_out, and_10_out);
  xor xor_10 (xor_10_out, in_14, in_13);
  and and_11 (and_11_out, or_7_out, in_13);
  xor xor_11 (xor_11_out, in_14, in_16);
  or or_8 (or_8_out, or_7_out, in_13);
  xor xor_12 (out_21, xor_10_out, or_7_out);
  and and_12 (and_12_out, xor_11_out, or_8_out);
  or or_9 (out_22, and_11_out, and_12_out);
endmodule
